# Fritzing sketch D_ports (saved by Fritzing 0.8.7b)
breadboards: 1

parts:
  Composant1 = Arduino Uno (Rev3)
  R1 = Resistor [tolerance=±5% resistance=100k package=THT]
  R2 = Resistor [tolerance=±5% resistance=100k package=THT]
  J1 = female pin header, 3 pins [form="♀ (female)"]
  J2 = female pin header, 3 pins [form="♀ (female)"]

nets:
  N1: Composant1.D10_PWM/SS, R2.Pin_0, J2.pin1
  N2: Composant1.D11_PWM/MOSI, R1.Pin_0, J1.pin1
  N3: Composant1.5V, J1.pin2, J2.pin3
  N4: Composant1.GND, R1.Pin_1, R2.Pin_1, J1.pin3, J2.pin2

notes:
  to D receiver
  from hub
