# Fritzing sketch Gas RPM sensor (saved by Fritzing 0.8.7b)
breadboards: 1

parts:
  Composant1 = Arduino Uno (Rev3)
  R1 = Resistor [tolerance=±5% resistance=22k package=THT]
  D1 = Rectifier Diode [part_number=1N4001 package="300 mil [THT]"]
  J1 = female pin header, 3 pins [form="♀ (female)"]
  J2 = female pin header, 3 pins [form="♀ (female)"]
  U1 = Optocoupler [package=THT]
  R2 = Resistor [tolerance=±5% resistance=1k package=THT]
  R3 = Resistor [tolerance=±5% resistance=10k package=THT]

nets:
  N1: Composant1.D10_PWM/SS, R1.Pin_0, D1.cathode
  N2: Composant1.D11_PWM/MOSI, D1.anode, J1.pin1
  N3: Composant1.D5_PWM, U1.Pin_4, R3.Pin_0
  N4: Composant1.5V, J1.pin2, R3.Pin_1
  N5: Composant1.GND, R1.Pin_1, J1.pin3, U1.Pin_5
  N6: J2.pin1, U1.Pin_2
  N7: J2.pin3, R2.Pin_1
  N8: U1.Pin_1, R2.Pin_0

notes:
  Smart Port
  Gas RPM sensor
  Pull-up 22kΩ
  Volt. red. 100 Ω
  Brushless sensor: pull-up 1kΩ
  Pull-down 10kΩ
